# Fritzing sketch Wiring diagram (saved by Fritzing 0.9.3b)
breadboards: 4

parts:
  Rx->Rx_Tx->Tx = Arduino Nano (Rev3.0)
  RX_Operates_3_3V_add_resistor = Bluetooth HC-05 Macho
  R1 = Resistor [tolerance=±5% resistance=220 package=THT]  # not connected
  R2 = Resistor [tolerance=±5% resistance=220 package=THT]  # not connected
  Part1 = Arduino Uno (Rev3)
  Rx->Rx_Tx->Tx1 = Arduino Nano (Rev3.0)
  RX_Operates_3_3V_add_resistor1 = Bluetooth HC-05 Macho
  R3 = Resistor [tolerance=±5% resistance=220 package=THT]
  R4 = Resistor [tolerance=±5% resistance=220 package=THT]
  VCC1 = Battery block 9V
  SMA1 = Inductor [package="400 mil [THT]"]
  SMA2 = Inductor [package="400 mil [THT]"]
  SMA3 = Inductor [package="400 mil [THT]"]
  SMA4 = Inductor [package="400 mil [THT]"]
  U1 = Voltage Regulator - 5V [package="TO220 [THT]"]
  R5 = Resistor [tolerance=±5% resistance=1 package=THT]
  R6 = Resistor [tolerance=±5% resistance=1k package=THT]
  VCC2 = Battery
  VCC3 = Battery

nets:
  N1: Rx->Rx_Tx->Tx.D1/TX, RX_Operates_3_3V_add_resistor.TXD
  VIN: Rx->Rx_Tx->Tx.VIN, Part1.5V, VCC1.+
  5V: Rx->Rx_Tx->Tx.5V, RX_Operates_3_3V_add_resistor.VCC
  N2: Rx->Rx_Tx->Tx.A5, Part1.A5/SCL
  N3: Rx->Rx_Tx->Tx.A4, Part1.A4/SDA
  GND: RX_Operates_3_3V_add_resistor.GND, Part1.GND, VCC1.-
  N4: Rx->Rx_Tx->Tx1.D1/TX, RX_Operates_3_3V_add_resistor1.TXD
  N5: Rx->Rx_Tx->Tx1.D0/RX, R4.Pin_1
  GND_2: Rx->Rx_Tx->Tx1.GND, RX_Operates_3_3V_add_resistor1.GND, SMA4.pin_1, U1.output_voltage, VCC3.-
  N6: Rx->Rx_Tx->Tx1.D5, R5.Pin_1
  VIN_2: Rx->Rx_Tx->Tx1.VIN, R3.Pin_0, U1.GND, R6.Pin_0, VCC2.+
  5V_2: Rx->Rx_Tx->Tx1.5V, RX_Operates_3_3V_add_resistor1.VCC
  N7: RX_Operates_3_3V_add_resistor1.RXD, R3.Pin_1, R4.Pin_0
  N8: SMA1.pin_0, R6.Pin_1
  N9: SMA1.pin_1, SMA2.pin_0
  N10: SMA2.pin_1, SMA3.pin_0
  N11: SMA3.pin_1, SMA4.pin_0
  N12: U1.input_voltage, R5.Pin_0

notes:
  Rx->Rx
  Tx->Tx
  3.3V Rx, add resistor
  VEHICLE CIRCUIT
  TIRE CIRCUIT
  SMA Circuit
